// Logisim project FilesAndImages.circ as structural Verilog: 1 circuit, main circuit main
module main (
);

  wire button_1_out, button_2_out, clock_1_out, clock_2_out;
  wire [7:0] fileviewer_1_p1, fileviewer_2_p1;

  Clock clock_1 (.out(clock_1_out));
  Button button_1 (.out(button_1_out));
  Clock clock_2 (.out(clock_2_out));
  Button button_2 (.out(button_2_out));
  // FileViewer #(.addrWidth(8), .lines(2)) fileviewer_1: pin names not known; wires that end beside it: fileviewer_1_p1
  Counter counter_1 (.Q(fileviewer_1_p1), .clk(clock_1_out), .clr(button_1_out));  // open: load, D, count, carry
  // FileViewer #(.addrWidth(8), .filename("caltech.txt"), .lines(2), .storage("link")) fileviewer_2: pin names not known; wires that end beside it: fileviewer_2_p1
  Counter counter_2 (.Q(fileviewer_2_p1), .clk(clock_2_out), .clr(button_2_out));  // open: load, D, count, carry

  // Notes on the sheet:
  //   contents of fileviewer_1 (hex, n*v repeats v):
  //   by Richard Brautigan  I don't care how God-damn smart these guys are: I'm bored.  It's been raining
  //   like hell all day long and there's nothing to do.  Written January 24, 1967 while poet-in-residence
  //   at the California Institute of Technology.
endmodule
